# Fritzing sketch Base PCB (saved by Fritzing 0.9.2b)
circuit board: 2.84009cm x 4.47793cm

parts:
  NRF24L01 = double row female pin header, 8 pins [form="♀ (female)"]
  Power = female pin header, 2 pins [form="♀ (female)"]
  R1 = Resistor [tolerance=±5% resistance=1M package=THT]
  R2 = Resistor [tolerance=±5% resistance=470k package=THT]
  DHT = female pin header, 4 pins [form="♀ (female)"]
  J1 = female pin header, 4 pins [form="♀ (female)"]
  J2 = female pin header, 4 pins [form="♀ (female)"]
  C1 = Electrolytic Capacitor [capacitance=4.7µF voltage=50V package="100 mil [THT, electrolytic]"]
  IC1 = IC, DIP package, 18 pins [chip_label=IC]
  J3 = female pin header, 2 pins [form="♀ (female)"]

nets:
  N1: NRF24L01.pin1, Power.pin1, R2.Pin_1, DHT.pin3, DHT.pin4, J1.pin4, J2.pin4, C1.-, IC1.pin1
  N2: NRF24L01.pin3, IC1.pin13
  N3: NRF24L01.pin4, IC1.pin12
  N4: NRF24L01.pin7, IC1.pin10
  N5: NRF24L01.pin8, DHT.pin1, J1.pin1, J2.pin1, C1.+
  N6: Power.pin2, R1.Pin_1, IC1.pin18
  N7: R1.Pin_0, R2.Pin_0, IC1.pin14
  N8: DHT.pin2, IC1.pin4
  N9: J1.pin2, J2.pin2, J3.pin2
  N10: J1.pin3, J2.pin3, J3.pin1
